// Logisim project CPU_Design.circ as structural Verilog
// greater
module Data_Path (
);

  wire and_1_out, and_2_out, Beq, Bgt, clock_1_out, equal, greater, Jump, or_1_out, undriven, undriven_2,
       undriven_3, undriven_4, undriven_5, undriven_6, undriven_8, undriven_9;
  wire [2:0] undriven_7;
  wire [3:0] multiplexer_3_out;
  wire [5:0] rom_1_data;
  wire [17:0] address;
  wire [23:0] adder_1_out, adder_2_out, alu_1_alu_output, bit_extender_1_out, bit_extender_2_out, Imm,
       multiplexer_1_out, multiplexer_2_out, multiplexer_6_out, ram_1_data, register_1_q,
       register_file_1_rs_out, register_file_1_rt_out;

  Clock clock_1 (.out(clock_1_out));
  Register #(.width(24)) register_1 (.D(multiplexer_2_out), .Q(register_1_q), .clk(clock_1_out));  // open: en, clr
  Adder #(.width(24)) adder_1 (.a(24'h3), .b(register_1_q), .out(adder_1_out));  // open: cin, cout
  and and_1 (and_1_out, greater, Bgt);
  and and_2 (and_2_out, equal, Beq);
  Adder #(.width(24)) adder_2 (.a(Imm), .b(adder_1_out), .out(adder_2_out));  // open: cin, cout
  Multiplexer #(.width(24), .enable("false")) multiplexer_1 (
    .in0(adder_1_out), .in1(adder_2_out), .out(multiplexer_1_out), .sel(or_1_out));
  or or_1 (or_1_out, and_1_out, and_2_out);
  ROM #(.addrWidth(24), .dataWidth(24)) rom_1 (.addr(register_1_q), .data({address, rom_1_data}));  // open: sel
  Multiplexer #(.width(24), .enable("false")) multiplexer_2 (
    .in0({adder_1_out[23:18], address}), .in1(multiplexer_1_out), .out(multiplexer_2_out), .sel(Jump));
  Control_Unit control_unit_1 ();
  assign bit_extender_1_out = {{14{1'b0}}, address[17:8]};  // Bit_Extender bit_extender_1
  assign bit_extender_2_out = {{14{address[17]}}, address[17:8]};  // Bit_Extender bit_extender_2
  Multiplexer #(.width(4), .enable("false")) multiplexer_3 (
    .in0(address[7:4]), .in1(address[11:8]), .out(multiplexer_3_out), .sel(undriven));
  Multiplexer #(.width(24), .enable("false")) multiplexer_4 (
    .in0(bit_extender_1_out), .in1(bit_extender_2_out), .out(Imm), .sel(undriven_4));
  Register_File register_file_1 (
    .RT(address[7:4]), .RD(multiplexer_3_out), .RS(address[3:0]), .Data_input(multiplexer_6_out),
    .RS_Out(register_file_1_rs_out), .RT_Out(register_file_1_rt_out), .register_write(undriven_5),
    .in_5(clock_1_out));
  Alu_Control alu_control_1 (.in_1(undriven_3));
  Multiplexer #(.width(24), .enable("false")) multiplexer_5 (
    .in0(register_file_1_rs_out), .in1(Imm), .sel(undriven_6));  // open: out
  ALU alu_1 (
    .in_1(register_file_1_rt_out), .ALU_Output(alu_1_alu_output), .greater(greater), .equal(equal),
    .ALU_Op(undriven_7));  // open: in_2
  RAM #(.addrWidth(24), .dataWidth(24), .bus("separate")) ram_1 (
    .addr(alu_1_alu_output), .din(register_file_1_rs_out), .data(ram_1_data), .str(undriven_8),
    .clk(clock_1_out), .ld(undriven_9));  // open: sel, clr
  Multiplexer #(.width(24), .enable("false")) multiplexer_6 (
    .in0(alu_1_alu_output), .in1(ram_1_data), .out(multiplexer_6_out), .sel(undriven_2));
endmodule

module Register_File (
  input  [3:0] RS,
  input  register_write,
  input  [3:0] RT,
  input  [3:0] RD,
  input  in_5,
  input  [23:0] Data_input,
  output [23:0] RS_Out,
  output [23:0] RT_Out
);

  wire demultiplexer_1_out0, demultiplexer_1_out1, demultiplexer_1_out2, demultiplexer_1_out3,
       demultiplexer_1_out4, demultiplexer_1_out5, demultiplexer_1_out6, demultiplexer_1_out7,
       demultiplexer_1_out8, demultiplexer_1_out9, demultiplexer_1_out10, demultiplexer_1_out11,
       demultiplexer_1_out12, demultiplexer_1_out13, demultiplexer_1_out14, demultiplexer_1_out15, undriven;
  wire [23:0] Reg1_q, Reg2_q, Reg3_q, Reg4_q, Reg5_q, Reg6_q, Reg7_q, Reg8_q, Reg9_q, Reg10_q, Reg11_q,
       Reg12_q, Reg13_q, Reg14_q, Reg15_q, Reg16_q;

  Demultiplexer #(.select(4)) demultiplexer_1 (
    .out0(demultiplexer_1_out0), .out1(demultiplexer_1_out1), .out2(demultiplexer_1_out2),
    .out3(demultiplexer_1_out3), .out4(demultiplexer_1_out4), .out5(demultiplexer_1_out5),
    .out6(demultiplexer_1_out6), .out7(demultiplexer_1_out7), .out8(demultiplexer_1_out8),
    .out9(demultiplexer_1_out9), .out10(demultiplexer_1_out10), .out11(demultiplexer_1_out11),
    .out12(demultiplexer_1_out12), .out13(demultiplexer_1_out13), .out14(demultiplexer_1_out14),
    .out15(demultiplexer_1_out15), .in(register_write), .sel(RD));  // open: en
  Register #(.width(24)) Reg1 (.D(Data_input), .en(demultiplexer_1_out0), .Q(Reg1_q), .clk(undriven));  // open: clr
  Register #(.width(24)) Reg2 (.D(Data_input), .en(demultiplexer_1_out1), .Q(Reg2_q), .clk(undriven));  // open: clr
  Register #(.width(24)) Reg3 (.D(Data_input), .en(demultiplexer_1_out2), .Q(Reg3_q), .clk(undriven));  // open: clr
  Register #(.width(24)) Reg4 (.D(Data_input), .en(demultiplexer_1_out3), .Q(Reg4_q), .clk(undriven));  // open: clr
  Register #(.width(24)) Reg5 (.D(Data_input), .en(demultiplexer_1_out4), .Q(Reg5_q), .clk(undriven));  // open: clr
  Register #(.width(24)) Reg6 (.D(Data_input), .en(demultiplexer_1_out5), .Q(Reg6_q), .clk(undriven));  // open: clr
  Register #(.width(24)) Reg7 (.D(Data_input), .en(demultiplexer_1_out6), .Q(Reg7_q), .clk(undriven));  // open: clr
  Register #(.width(24)) Reg8 (.D(Data_input), .en(demultiplexer_1_out7), .Q(Reg8_q), .clk(undriven));  // open: clr
  Register #(.width(24)) Reg9 (.D(Data_input), .en(demultiplexer_1_out8), .Q(Reg9_q), .clk(undriven));  // open: clr
  Register #(.width(24)) Reg10 (.D(Data_input), .en(demultiplexer_1_out9), .Q(Reg10_q), .clk(undriven));  // open: clr
  Register #(.width(24)) Reg11 (.D(Data_input), .en(demultiplexer_1_out10), .Q(Reg11_q), .clk(undriven));  // open: clr
  Register #(.width(24)) Reg12 (.D(Data_input), .en(demultiplexer_1_out11), .Q(Reg12_q), .clk(undriven));  // open: clr
  Register #(.width(24)) Reg13 (.D(Data_input), .en(demultiplexer_1_out12), .Q(Reg13_q), .clk(undriven));  // open: clr
  Register #(.width(24)) Reg14 (.D(Data_input), .en(demultiplexer_1_out13), .Q(Reg14_q), .clk(undriven));  // open: clr
  Register #(.width(24)) Reg15 (.D(Data_input), .en(demultiplexer_1_out14), .Q(Reg15_q), .clk(undriven));  // open: clr
  Register #(.width(24)) Reg16 (.D(Data_input), .en(demultiplexer_1_out15), .Q(Reg16_q), .clk(undriven));  // open: clr
  Multiplexer #(.select(4), .width(24), .enable("false")) multiplexer_1 (
    .in0(Reg1_q), .in1(Reg2_q), .in2(Reg3_q), .in3(Reg4_q), .in4(Reg5_q), .in5(Reg6_q), .in6(Reg7_q),
    .in7(Reg8_q), .in8(Reg9_q), .in9(Reg10_q), .in10(Reg11_q), .in11(Reg12_q), .in12(Reg13_q),
    .in13(Reg14_q), .in14(Reg15_q), .in15(Reg16_q), .out(RS_Out), .sel(RS));
  Multiplexer #(.select(4), .width(24), .enable("false")) multiplexer_2 (
    .in0(Reg1_q), .in1(Reg2_q), .in2(Reg3_q), .in3(Reg4_q), .in4(Reg5_q), .in5(Reg6_q), .in6(Reg7_q),
    .in7(Reg8_q), .in8(Reg9_q), .in9(Reg10_q), .in10(Reg11_q), .in11(Reg12_q), .in12(Reg13_q),
    .in13(Reg14_q), .in14(Reg15_q), .in15(Reg16_q), .out(RT_Out), .sel(RT));

  // Notes on the sheet:
  //   register write
endmodule

module ALU (
  input  [23:0] in_1,
  input  [23:0] in_2,
  input  [2:0] ALU_Op,
  output [23:0] ALU_Output,
  output greater,
  output equal
);

  wire [23:0] adder_1_out, and_1_out, divider_1_out, multiplier_1_out, or_1_out, shifter_1_out,
       shifter_2_out, subtractor_1_out;

  assign and_1_out = in_1 & in_2;  // AND_Gate and_1, 24 bits wide
  assign or_1_out = in_1 | in_2;  // OR_Gate or_1, 24 bits wide
  Adder #(.width(24)) adder_1 (.a(in_1), .b(in_2), .out(adder_1_out));  // open: cin, cout
  Subtractor #(.width(24)) subtractor_1 (.a(in_1), .b(in_2), .out(subtractor_1_out));  // open: bin, bout
  Multiplier #(.width(24)) multiplier_1 (.a(in_1), .b(in_2), .out(multiplier_1_out));  // open: cin, cout
  Divider #(.width(24)) divider_1 (.a(in_1), .b(in_2), .out(divider_1_out));  // open: upper, rem
  Shifter #(.width(24)) shifter_1 (.in(in_1), .\dist (in_2[4:0]), .out(shifter_1_out));
  Shifter #(.width(24), .shift("ar")) shifter_2 (.in(in_1), .\dist (in_2[4:0]), .out(shifter_2_out));
  Multiplexer #(.select(3), .width(24), .enable("false")) multiplexer_1 (
    .in0(and_1_out), .in1(or_1_out), .in2(adder_1_out), .in3(subtractor_1_out), .in4(multiplier_1_out),
    .in5(divider_1_out), .in6(shifter_1_out), .in7(shifter_2_out), .out(ALU_Output), .sel(ALU_Op));
  Comparator #(.width(24)) comparator_1 (.a(ALU_Output), .b({24{1'b0}}), .gt(greater), .eq(equal));  // open: lt
endmodule

module Alu_Control (
  input  in_1
);
endmodule
